# Fritzing sketch zoom-controller-schematic (saved by Fritzing 0.9.4)
breadboards: 1

parts:
  Part1 = Arduino Micro (Rev3)
  S1 = Pushbutton [package="[THT]"]
  S2 = Pushbutton [package="[THT]"]
  R1 = Resistor [tolerance=±1% resistance=10k package=THT]
  R2 = Resistor [tolerance=±1% resistance=10k package=THT]

nets:
  N1: Part1.D5_PWM, S1.Pin_3, S1.Pin_4, R1.Pin_1
  N2: Part1.D8_PWM/A8, S2.Pin_3, S2.Pin_4, R2.Pin_1
  N3: Part1.GND, R1.Pin_0, R2.Pin_0
  N4: Part1.5V, S1.Pin_1, S1.Pin_2, S2.Pin_1, S2.Pin_2
